# Fritzing sketch BuzzerPiano (saved by Fritzing 0.9.3b)
breadboards: 1

parts:
  R3 = Resistor [tolerance=±5% resistance=100k package=THT]
  R4 = Resistor [tolerance=±5% resistance=100k package=THT]
  R5 = Resistor [tolerance=±5% resistance=100k package=THT]
  R6 = Resistor [tolerance=±5% resistance=100k package=THT]
  R7 = Resistor [tolerance=±5% resistance=100k package=THT]
  R8 = Resistor [tolerance=±5% resistance=100k package=THT]
  R9 = Resistor [tolerance=±5% resistance=100k package=THT]
  S2 = Pushbutton [package="[THT]"]
  S3 = Pushbutton [package="[THT]"]
  S4 = Pushbutton [package="[THT]"]
  S5 = Pushbutton [package="[THT]"]
  S6 = Pushbutton [package="[THT]"]
  S7 = Pushbutton [package="[THT]"]
  S8 = Pushbutton [package="[THT]"]
  LED1 = LED - 5mm [color="White (6500K)" package="5 mm [THT]"]
  LED2 = LED - 5mm [color="White (6500K)" package="5 mm [THT]"]
  LED3 = LED - 5mm [color="White (6500K)" package="5 mm [THT]"]
  LED4 = LED - 5mm [color="White (6500K)" package="5 mm [THT]"]
  LED5 = LED - 5mm [color="White (6500K)" package="5 mm [THT]"]
  LED7 = LED - 5mm [color="White (6500K)" package="5 mm [THT]"]
  LED8 = LED - 5mm [color="White (6500K)" package="5 mm [THT]"]
  J1 = Piezo Speaker
  Part1 = Arduino Uno (Rev3)

nets:
  N1: R3.Pin_0, R4.Pin_0, R5.Pin_0, R6.Pin_0, R7.Pin_0, R9.Pin_0, J1.pin1, Part1.GND
  N2: R3.Pin_1, S7.Pin_1, S7.Pin_2, Part1.D10_PWM/SS
  N3: R4.Pin_1, S4.Pin_1, S4.Pin_2, Part1.D7
  N4: R5.Pin_1, S6.Pin_1, S6.Pin_2, Part1.D8
  N5: R6.Pin_1, S8.Pin_1, S8.Pin_2, Part1.D9_PWM
  N6: R7.Pin_1, S2.Pin_1, S2.Pin_2, Part1.D4
  N7: R8.Pin_1, S3.Pin_1, S3.Pin_2, Part1.D5_PWM
  N8: R9.Pin_1, S5.Pin_1, S5.Pin_2, Part1.D6_PWM
  N9: S2.Pin_3, S2.Pin_4, LED1.cathode
  N10: S3.Pin_3, S3.Pin_4, LED2.cathode
  N11: S4.Pin_3, S4.Pin_4, LED4.cathode
  N12: S5.Pin_3, S5.Pin_4, LED3.cathode
  N13: S6.Pin_3, S6.Pin_4, LED5.cathode
  N14: S7.Pin_3, S7.Pin_4, LED8.cathode
  N15: S8.Pin_3, S8.Pin_4, LED7.cathode
  N16: LED1.anode, LED2.anode, LED3.anode, LED4.anode, LED5.anode, LED8.anode, Part1.5V
  N17: J1.pin2, Part1.D11_PWM/MOSI
